// Logisim project TARA16.circ as structural Verilog: 33 circuits, main circuit main
module main (
  input  CLK,
  input  RST,
  output Z,
  output N,
  output C,
  output V
);

  wire control_rom_1_alu_out, control_rom_1_clock, control_rom_1_ir_load, control_rom_1_mar_load,
       control_rom_1_mdr_load, control_rom_1_mdr_select, control_rom_1_mem_read, control_rom_1_mem_write,
       control_rom_1_pc_add, control_rom_1_pc_inc, control_rom_1_pc_load, control_rom_1_regfile_load,
       control_rom_1_reset, control_rom_1_status_load;
  wire [3:0] control_rom_1_bus_source;
  wire [4:0] control_rom_1_alu_select, datapath_1_opcode;
  wire [15:0] datapath_1_bus_out;

  Control_ROM control_rom_1 (
    .Z(Z), .N(N), .CLK(CLK), .OPCODE(datapath_1_opcode), .RST(RST), .ALU_select(control_rom_1_alu_select),
    .PC_load(control_rom_1_pc_load), .PC_inc(control_rom_1_pc_inc), .PC_add(control_rom_1_pc_add),
    .MAR_load(control_rom_1_mar_load), .MDR_select(control_rom_1_mdr_select),
    .MDR_load(control_rom_1_mdr_load), .IR_load(control_rom_1_ir_load),
    .Regfile_load(control_rom_1_regfile_load), .Alu_out(control_rom_1_alu_out),
    .Status_load(control_rom_1_status_load), .Mem_read(control_rom_1_mem_read),
    .Mem_write(control_rom_1_mem_write), .clock(control_rom_1_clock), .reset(control_rom_1_reset),
    .Bus_source(control_rom_1_bus_source));
  datapath datapath_1 (
    .ALU_select(control_rom_1_alu_select), .PC_load(control_rom_1_pc_load),
    .PC_increment(control_rom_1_pc_inc), .PC_add(control_rom_1_pc_add), .MAR_Load(control_rom_1_mar_load),
    .MDR_select(control_rom_1_mdr_select), .MDR_load(control_rom_1_mdr_load),
    .IR_load(control_rom_1_ir_load), .Regfile_load(control_rom_1_regfile_load),
    .ALU_output(control_rom_1_alu_out), .Status_load(control_rom_1_status_load),
    .Mem_read(control_rom_1_mem_read), .Mem_write(control_rom_1_mem_write), .CLK(control_rom_1_clock),
    .RST(control_rom_1_reset), .BUS_SOURCE(control_rom_1_bus_source), .Opcode(datapath_1_opcode),
    .BUS_out(datapath_1_bus_out), .Z(Z), .N(N), .C(C), .V(V));  // open: EN_OUT, BUS_IN
endmodule

module byteregister (
  input  [7:0] D_byte,
  input  CLK,
  input  EN,
  input  RST,
  output [7:0] Q_byte
);

  dff dff_1 (.D(D_byte[0]), .CLK(CLK), .EN(EN), .RST(RST), .Q(Q_byte[0]));
  dff dff_2 (.D(D_byte[1]), .CLK(CLK), .EN(EN), .RST(RST), .Q(Q_byte[1]));
  dff dff_3 (.D(D_byte[2]), .CLK(CLK), .EN(EN), .RST(RST), .Q(Q_byte[2]));
  dff dff_4 (.D(D_byte[3]), .CLK(CLK), .EN(EN), .RST(RST), .Q(Q_byte[3]));
  dff dff_5 (.D(D_byte[4]), .CLK(CLK), .EN(EN), .RST(RST), .Q(Q_byte[4]));
  dff dff_6 (.D(D_byte[5]), .CLK(CLK), .EN(EN), .RST(RST), .Q(Q_byte[5]));
  dff dff_7 (.D(D_byte[6]), .CLK(CLK), .EN(EN), .RST(RST), .Q(Q_byte[6]));
  dff dff_8 (.D(D_byte[7]), .CLK(CLK), .EN(EN), .RST(RST), .Q(Q_byte[7]));

  // Notes on the sheet:
  //   CS25B031
  //   CS25B067
endmodule

module register16 (
  input  [15:0] D,
  input  CLK,
  input  LOAD,
  input  RST,
  output [15:0] Q
);

  byteregister byteregister_1 (.D_byte(D[7:0]), .CLK(CLK), .EN(LOAD), .RST(RST), .Q_byte(Q[7:0]));
  byteregister byteregister_2 (.D_byte(D[15:8]), .CLK(CLK), .EN(LOAD), .RST(RST), .Q_byte(Q[15:8]));

  // Notes on the sheet:
  //   CS25B031
  //   CS25B067
endmodule

module regfile8x16 (
  input  [2:0] RA,
  input  [2:0] RB,
  input  [2:0] RD,
  input  [15:0] DIN,
  input  WE,
  input  CLK,
  input  RST,
  output [15:0] QA,
  output [15:0] QB,
  output [15:0] R0,
  output [15:0] R1,
  output [15:0] R2,
  output [15:0] R3,
  output [15:0] R4,
  output [15:0] R5,
  output [15:0] R6,
  output [15:0] R7
);

  wire decoder_1_out0, decoder_1_out1, decoder_1_out2, decoder_1_out3, decoder_1_out4, decoder_1_out5,
       decoder_1_out6, decoder_1_out7;

  Decoder #(.select(3)) decoder_1 (
    .out0(decoder_1_out0), .out1(decoder_1_out1), .out2(decoder_1_out2), .out3(decoder_1_out3),
    .out4(decoder_1_out4), .out5(decoder_1_out5), .out6(decoder_1_out6), .out7(decoder_1_out7), .sel(RD),
    .en(WE));
  register16 register16_1 (.D(DIN), .CLK(CLK), .LOAD(decoder_1_out0), .RST(RST), .Q(R0));
  register16 register16_2 (.D(DIN), .CLK(CLK), .LOAD(decoder_1_out1), .RST(RST), .Q(R1));
  register16 register16_3 (.D(DIN), .CLK(CLK), .LOAD(decoder_1_out2), .RST(RST), .Q(R2));
  register16 register16_4 (.D(DIN), .CLK(CLK), .LOAD(decoder_1_out3), .RST(RST), .Q(R3));
  register16 register16_5 (.D(DIN), .CLK(CLK), .LOAD(decoder_1_out4), .RST(RST), .Q(R4));
  register16 register16_6 (.D(DIN), .CLK(CLK), .LOAD(decoder_1_out5), .RST(RST), .Q(R5));
  register16 register16_7 (.D(DIN), .CLK(CLK), .LOAD(decoder_1_out6), .RST(RST), .Q(R6));
  register16 register16_8 (.D(DIN), .CLK(CLK), .LOAD(decoder_1_out7), .RST(RST), .Q(R7));
  Multiplexer #(.select(3), .width(16)) multiplexer_1 (
    .in0(R0), .in1(R1), .in2(R2), .in3(R3), .in4(R4), .in5(R5), .in6(R6), .in7(R7), .out(QA), .sel(RA));
  Multiplexer #(.select(3), .width(16)) multiplexer_2 (
    .in0(R0), .in1(R1), .in2(R2), .in3(R3), .in4(R4), .in5(R5), .in6(R6), .in7(R7), .out(QB), .sel(RB));

  // Notes on the sheet:
  //   CS25B031
  //   CS25B067
endmodule

module status_reg (
  input  Z_IN,
  input  N_IN,
  input  C_IN,
  input  V_IN,
  input  STATUS_WE,
  input  CLK,
  input  RST,
  output Z,
  output N,
  output C,
  output V
);

  dff dff_1 (.D(Z_IN), .CLK(CLK), .EN(STATUS_WE), .RST(RST), .Q(Z));
  dff dff_2 (.D(N_IN), .CLK(CLK), .EN(STATUS_WE), .RST(RST), .Q(N));
  dff dff_3 (.D(C_IN), .CLK(CLK), .EN(STATUS_WE), .RST(RST), .Q(C));
  dff dff_4 (.D(V_IN), .CLK(CLK), .EN(STATUS_WE), .RST(RST), .Q(V));

  // Notes on the sheet:
  //   CS25B031
  //   CS25B067
endmodule

module ram_word (
  input  [15:0] ADDR,
  input  [15:0] DIN,
  input  MEM_READ,
  input  MEM_WRITE,
  input  CLK,
  input  is_byte,
  input  is_store,
  output [15:0] DOUT
);

  wire and_1_out, and_2_out, and_3_out, multiplexer_1_out, multiplexer_2_out, not_1_out;
  wire [7:0] ram_1_dout, ram_2_dout;

  and and_1 (and_1_out, is_byte, is_store);
  not not_1 (not_1_out, ADDR[0]);
  Multiplexer multiplexer_1 (.in0(MEM_WRITE), .in1(1'b0), .out(multiplexer_1_out), .sel(and_2_out));
  and and_2 (and_2_out, not_1_out, and_1_out);
  Multiplexer multiplexer_2 (.in0(MEM_WRITE), .in1(1'b0), .out(multiplexer_2_out), .sel(and_3_out));
  and and_3 (and_3_out, ADDR[0], and_1_out);
  RAM #(.addrWidth(15), .asyncread("true")) ram_1 (
    .addr(ADDR[15:1]), .we(multiplexer_1_out), .oe(MEM_READ), .clk(CLK), .din(DIN[7:0]), .dout(ram_1_dout));
  RAM #(.addrWidth(15), .asyncread("true")) ram_2 (
    .addr(ADDR[15:1]), .we(multiplexer_2_out), .oe(MEM_READ), .clk(CLK), .din(DIN[15:8]), .dout(ram_2_dout));
  assign DOUT = MEM_READ ? {ram_2_dout, ram_1_dout} : 16'bz;  // Controlled_Buffer controlled_buffer_1

  // Notes on the sheet:
  //   CS25B031
  //   CS25B067
endmodule

module datapath (
  input  [4:0] ALU_select,
  input  PC_load,
  input  PC_increment,
  input  PC_add,
  input  MAR_Load,
  input  MDR_select,
  input  MDR_load,
  input  IR_load,
  input  Regfile_load,
  input  ALU_output,
  input  Status_load,
  input  Mem_read,
  input  Mem_write,
  input  CLK,
  input  RST,
  input  EN_OUT,
  input  [3:0] BUS_SOURCE,
  input  [15:0] BUS_IN,
  output [4:0] Opcode,
  output [15:0] BUS_out,
  output Z,
  output N,
  output C,
  output V
);

  wire addr_parity, alu_1_carry, alu_1_negative, alu_1_overflow, alu_1_zero, and_2_out, and_5_out,
       comparator_7_eq, comparator_8_eq, decoder_1_out0, decoder_1_out1, decoder_1_out2, decoder_1_out3,
       decoder_1_out4, decoder_1_out5, decoder_1_out6, decoder_1_out7, decoder_1_out8, decoder_1_out9, is_2,
       is_7, is_addi, is_branch, is_byte, is_lors, is_pop, is_push, is_shift, is_stack, is_store, lnots,
       N_temp, not_1_out, not_2_out, not_3_out, not_4_out, not_5_out, not_6_out, not_8_out, or_1_out,
       or_2_out, status_reg_1_n, status_reg_1_z, xor_1_out, Z_temp;
  wire [2:0] fmt, multiplexer_12_out, tara_decoder_1_ra, tara_decoder_1_rb, tara_decoder_1_rd;
  wire [4:0] tara_decoder_1_off5;
  wire [7:0] multiplexer_5_out, tara_decoder_1_imm8, tara_decoder_1_rel8;
  wire [10:0] tara_decoder_1_rel11;
  wire [14:0] multiplexer_13_out;
  wire [15:0] alu_1_bus_out, alu_acc_q, bit_extender_1_out, bit_extender_2_out, controlled_buffer_1_out,
       controlled_buffer_2_out, controlled_buffer_5_out, controlled_buffer_6_out, controlled_buffer_9_out,
       imm8, ir_1_ir_out, mdr_in, mdr_out, multiplexer_1_out, multiplexer_2_out, multiplexer_3_out,
       multiplexer_4_out, multiplexer_6_out, multiplexer_7_out, multiplexer_8_out, off5, pc_1_q, QA, QB,
       ram_word_1_dout, regfile8x16_1_r0, regfile8x16_1_r1, regfile8x16_1_r2, regfile8x16_1_r3,
       regfile8x16_1_r4, regfile8x16_1_r5, regfile8x16_1_r6, regfile8x16_1_r7;
  wire [15:1] mar_1_mar_out;
  wire [15:15] multiplexer_13_out_2;

  not not_1 (not_1_out, MDR_select);
  not not_2 (not_2_out, EN_OUT);
  and and_1 (lnots, not_1_out, MDR_load);
  Decoder #(.select(4)) decoder_1 (
    .out0(decoder_1_out0), .out1(decoder_1_out1), .out2(decoder_1_out2), .out3(decoder_1_out3),
    .out4(decoder_1_out4), .out5(decoder_1_out5), .out6(decoder_1_out6), .out7(decoder_1_out7),
    .out8(decoder_1_out8), .out9(decoder_1_out9), .sel(BUS_SOURCE), .en(not_2_out));  // open: out10, out11, out12, out13, out14, out15
  assign controlled_buffer_1_out = Regfile_load ? BUS_out : 16'bz;  // Controlled_Buffer controlled_buffer_1
  regfile8x16 regfile8x16_1 (
    .RA(tara_decoder_1_ra), .RB(tara_decoder_1_rb), .RD(multiplexer_12_out), .DIN(controlled_buffer_1_out),
    .WE(Regfile_load), .CLK(CLK), .RST(RST), .QA(QA), .QB(QB), .R0(regfile8x16_1_r0), .R1(regfile8x16_1_r1),
    .R2(regfile8x16_1_r2), .R3(regfile8x16_1_r3), .R4(regfile8x16_1_r4), .R5(regfile8x16_1_r5),
    .R6(regfile8x16_1_r6), .R7(regfile8x16_1_r7));
  // Probe on regfile8x16_1_r0
  // Probe on regfile8x16_1_r1
  // Probe on regfile8x16_1_r2
  // Probe on regfile8x16_1_r3
  // Probe on regfile8x16_1_r4
  // Probe on regfile8x16_1_r5
  // Probe on regfile8x16_1_r6
  // Probe on regfile8x16_1_r7
  assign controlled_buffer_2_out = PC_load ? BUS_out : 16'bz;  // Controlled_Buffer controlled_buffer_2
  Comparator #(.width(16)) comparator_1 (.a(QA), .b({16{1'b0}}), .eq(Z_temp), .lt(N_temp));  // open: gt
  assign BUS_out = decoder_1_out3 ? QA : 16'bz;  // Controlled_Buffer controlled_buffer_3
  Multiplexer #(.width(16)) multiplexer_1 (.in0({16{1'b0}}), .in1(16'h2), .out(multiplexer_1_out), .sel(is_2));
  Multiplexer #(.width(16)) multiplexer_2 (
    .in0(multiplexer_1_out), .in1(imm8), .out(multiplexer_2_out), .sel(or_1_out));
  or or_1 (or_1_out, is_addi, is_shift);
  PC pc_1 (
    .D(controlled_buffer_2_out), .CLK(CLK), .LOAD(PC_load), .RST(RST), .INCREMENT(PC_increment),
    .Rel11({multiplexer_13_out, 1'b0}), .Add(PC_add), .Q(pc_1_q));
  assign BUS_out = decoder_1_out0 ? pc_1_q : 16'bz;  // Controlled_Buffer controlled_buffer_4
  Multiplexer #(.width(16)) multiplexer_3 (.in0(QA), .in1(off5), .out(multiplexer_3_out), .sel(is_lors));
  Multiplexer #(.width(16)) multiplexer_4 (.in0(QB), .in1(multiplexer_2_out), .out(multiplexer_4_out), .sel(or_2_out));
  or or_2 (or_2_out, or_1_out, is_2, is_branch);
  // Probe on pc_1_q
  assign controlled_buffer_5_out = MAR_Load ? BUS_out : 16'bz;  // Controlled_Buffer controlled_buffer_5
  alu alu_1 (
    .A(multiplexer_3_out), .B(multiplexer_4_out), .ALU_OUTPUT_ENABLE(ALU_output), .OPCODE(ALU_select),
    .ZERO(alu_1_zero), .NEGATIVE(alu_1_negative), .CARRY(alu_1_carry), .OVERFLOW(alu_1_overflow),
    .BUS_OUT(alu_1_bus_out));
  // Probe on mdr_in
  Multiplexer #(.width(8)) multiplexer_5 (
    .in0(mdr_in[7:0]), .in1(mdr_in[15:8]), .out(multiplexer_5_out), .sel(not_3_out));
  not not_3 (not_3_out, addr_parity);
  Multiplexer #(.width(16)) multiplexer_6 (
    .in0({QA[7:0], mdr_in[7:0]}), .in1({mdr_in[15:8], QA[7:0]}), .out(multiplexer_6_out), .sel(addr_parity));
  MAR mar_1 (
    .MAR_IN(controlled_buffer_5_out), .CLK(CLK), .LOAD(MAR_Load), .RST(RST),
    .MAR_OUT({mar_1_mar_out, addr_parity}));
  // Probe on {mar_1_mar_out, addr_parity}
  assign controlled_buffer_6_out = MDR_load ? multiplexer_8_out : 16'bz;  // Controlled_Buffer controlled_buffer_6
  assign BUS_out = decoder_1_out8 ? alu_acc_q : 16'bz;  // Controlled_Buffer controlled_buffer_7
  register16 alu_acc (.D(alu_1_bus_out), .CLK(CLK), .LOAD(ALU_output), .RST(RST), .Q(alu_acc_q));
  status_reg status_reg_1 (
    .Z_IN(alu_1_zero), .N_IN(alu_1_negative), .C_IN(alu_1_carry), .V_IN(alu_1_overflow),
    .STATUS_WE(Status_load), .CLK(CLK), .RST(RST), .Z(status_reg_1_z), .N(status_reg_1_n), .C(C), .V(V));
  Multiplexer #(.width(16)) multiplexer_7 (
    .in0({{8{1'b0}}, multiplexer_5_out}), .in1(multiplexer_6_out), .out(multiplexer_7_out), .sel(is_store));
  Multiplexer #(.width(16)) multiplexer_8 (.in0(BUS_out), .in1(QB), .out(multiplexer_8_out), .sel(is_push));
  Multiplexer #(.width(16)) multiplexer_9 (.in0(mdr_in), .in1(multiplexer_7_out), .out(mdr_out), .sel(and_2_out));
  and and_2 (and_2_out, is_lors, not_4_out, is_byte);
  not not_4 (not_4_out, IR_load);
  MDR mdr_1 (
    .BUS_OUT(controlled_buffer_6_out), .RAM_OUT(ram_word_1_dout), .MDR_SELECT(MDR_select), .CLK(CLK),
    .LOAD(MDR_load), .RST(RST), .Q(mdr_in));
  assign BUS_out = decoder_1_out1 ? mdr_out : 16'bz;  // Controlled_Buffer controlled_buffer_8
  // Probe on BUS_out
  Multiplexer multiplexer_10 (.in0(status_reg_1_z), .in1(Z_temp), .out(Z), .sel(is_branch));
  Multiplexer multiplexer_11 (.in0(status_reg_1_n), .in1(N_temp), .out(N), .sel(is_branch));
  ram_word ram_word_1 (
    .ADDR({mar_1_mar_out, addr_parity}), .DIN(mdr_out), .MEM_READ(Mem_read), .MEM_WRITE(Mem_write),
    .CLK(CLK), .is_byte(is_byte), .is_store(is_store), .DOUT(ram_word_1_dout));
  and and_3 (is_pop, is_stack, not_5_out);
  not not_5 (not_5_out, Opcode[0]);
  and and_4 (is_push, Opcode[0], is_stack);
  assign controlled_buffer_9_out = IR_load ? BUS_out : 16'bz;  // Controlled_Buffer controlled_buffer_9
  // Probe on ram_word_1_dout
  and and_5 (and_5_out, is_pop, ALU_output);
  IR ir_1 (.MDR_OUT(controlled_buffer_9_out), .CLK(CLK), .LOAD(IR_load), .RST(RST), .IR_OUT(ir_1_ir_out));
  assign BUS_out = decoder_1_out2 ? ir_1_ir_out : 16'bz;  // Controlled_Buffer controlled_buffer_10
  // Probe on ir_1_ir_out
  D_Flip_Flop d_ff_1 (.D(and_5_out), .clk(not_6_out), .Q(is_7), .reset(MAR_Load));  // open: Qn, preset
  not not_6 (not_6_out, CLK);
  Multiplexer #(.width(3)) multiplexer_12 (.in0(tara_decoder_1_rd), .in1(3'b111), .out(multiplexer_12_out), .sel(is_7));
  tara_decoder tara_decoder_1 (
    .IR(ir_1_ir_out), .opcode(Opcode), .RD(tara_decoder_1_rd), .RA(tara_decoder_1_ra),
    .RB(tara_decoder_1_rb), .IMM8(tara_decoder_1_imm8), .OFF5(tara_decoder_1_off5),
    .REL8(tara_decoder_1_rel8), .REL11(tara_decoder_1_rel11), .Format(fmt));
  assign bit_extender_1_out = {{5{tara_decoder_1_rel11[10]}}, tara_decoder_1_rel11};  // Bit_Extender bit_extender_1
  Multiplexer #(.width(16)) multiplexer_13 (
    .in0(bit_extender_1_out), .in1(bit_extender_2_out), .out({multiplexer_13_out_2[15], multiplexer_13_out}),
    .sel(is_branch));
  assign bit_extender_2_out = {{8{tara_decoder_1_rel8[7]}}, tara_decoder_1_rel8};  // Bit_Extender bit_extender_2
  assign BUS_out = decoder_1_out7 ? bit_extender_1_out : 16'bz;  // Controlled_Buffer controlled_buffer_11
  assign BUS_out = decoder_1_out6 ? bit_extender_2_out : 16'bz;  // Controlled_Buffer controlled_buffer_12
  assign off5 = {{11{tara_decoder_1_off5[4]}}, tara_decoder_1_off5};  // Bit_Extender bit_extender_3
  assign BUS_out = decoder_1_out5 ? off5 : 16'bz;  // Controlled_Buffer controlled_buffer_13
  assign imm8 = {{8{tara_decoder_1_imm8[7]}}, tara_decoder_1_imm8};  // Bit_Extender bit_extender_4
  assign BUS_out = decoder_1_out4 ? {{8{1'b0}}, tara_decoder_1_imm8} : 16'bz;  // Controlled_Buffer controlled_buffer_14
  Comparator #(.width(3)) comparator_2 (.a(3'b100), .b(fmt), .eq(is_lors));  // open: gt, lt
  Comparator #(.width(3)) comparator_3 (.a(3'b111), .b(fmt), .eq(is_stack));  // open: gt, lt
  Comparator #(.mode("unsigned"), .width(3)) comparator_4 (.a(3'b101), .b(fmt), .lt(is_2));  // open: gt, eq
  Comparator #(.width(3)) comparator_5 (.a(3'b101), .b(fmt), .eq(is_branch));  // open: gt, lt
  Comparator #(.width(5)) comparator_6 (.a(5'b01011), .b(Opcode), .eq(is_addi));  // open: gt, lt
  assign BUS_out = not_8_out ? BUS_IN : 16'bz;  // Controlled_Buffer controlled_buffer_15
  not not_7 (is_store, Opcode[0]);
  xor xor_1 (xor_1_out, Opcode[0], Opcode[1]);
  not not_8 (not_8_out, not_2_out);
  not not_9 (is_byte, xor_1_out);
  Comparator #(.width(5)) comparator_7 (.a(5'b10001), .b(Opcode), .eq(comparator_7_eq));  // open: gt, lt
  Comparator #(.width(5)) comparator_8 (.a(5'b10010), .b(Opcode), .eq(comparator_8_eq));  // open: gt, lt
  or or_3 (is_shift, comparator_7_eq, comparator_8_eq);
  assign BUS_out = decoder_1_out9 ? {tara_decoder_1_imm8, QA[7:0]} : 16'bz;  // Controlled_Buffer controlled_buffer_16

  // Other names for the same wires on the sheet: alu_load = ALU_output; is_fetch = IR_load;
  //   leastsigopcode = Opcode[0]

  // Notes on the sheet:
  //   REL11 : 0111
  //   ALU_OUT : 1000
  //   LIH_IN : 1001
  //   PC : 0000
  //   MDR : 0001
  //   IR : 0010
  //   REG_FILE : 0011
  //   IMM8 : 0100
  //   OFF5 : 0101
  //   REL8 : 0110
  //   POP reg_file load register hardcoded to 7
endmodule

module PC (
  input  [15:0] D,
  input  CLK,
  input  LOAD,
  input  RST,
  input  INCREMENT,
  input  [15:0] Rel11,
  input  Add,
  output [15:0] Q
);

  wire [15:0] adder16_1_s_16, multiplexer_1_out, multiplexer_2_out;

  Multiplexer #(.width(16)) multiplexer_1 (.in0(D), .in1(adder16_1_s_16), .out(multiplexer_1_out), .sel(INCREMENT));
  register16 register16_1 (.D(multiplexer_1_out), .CLK(CLK), .LOAD(LOAD), .RST(RST), .Q(Q));
  Multiplexer #(.width(16)) multiplexer_2 (.in0(16'h2), .in1(Rel11), .out(multiplexer_2_out), .sel(Add));
  adder16 adder16_1 (.CIN(1'b0), .A_16(Q), .B_16(multiplexer_2_out), .S_16(adder16_1_s_16));  // open: COUT

  // Notes on the sheet:
  //   CS25B031
  //   CS25B067
endmodule

module MAR (
  input  [15:0] MAR_IN,
  input  CLK,
  input  LOAD,
  input  RST,
  output [15:0] MAR_OUT
);

  register16 register16_1 (.D(MAR_IN), .CLK(CLK), .LOAD(LOAD), .RST(RST), .Q(MAR_OUT));

  // Notes on the sheet:
  //   CS25B031
  //   CS25B067
endmodule

module MDR (
  input  [15:0] BUS_OUT,
  input  [15:0] RAM_OUT,
  input  MDR_SELECT,
  input  CLK,
  input  LOAD,
  input  RST,
  output [15:0] Q
);

  wire [15:0] multiplexer_1_out;

  Multiplexer #(.width(16)) multiplexer_1 (.in0(BUS_OUT), .in1(RAM_OUT), .out(multiplexer_1_out), .sel(MDR_SELECT));
  Register #(.width(16)) register_1 (.D(multiplexer_1_out), .en(LOAD), .clk(CLK), .Q(Q), .clr(RST));

  // Notes on the sheet:
  //   CS25B031
  //   CS25B067
endmodule

module IR (
  input  [15:0] MDR_OUT,
  input  CLK,
  input  LOAD,
  input  RST,
  output [15:0] IR_OUT
);

  register16 register16_1 (.D(MDR_OUT), .CLK(CLK), .LOAD(LOAD), .RST(RST), .Q(IR_OUT));

  // Notes on the sheet:
  //   CS25B031
  //   CS25B067
endmodule

module alu (
  input  [15:0] A,
  input  [15:0] B,
  input  ALU_OUTPUT_ENABLE,
  input  [4:0] OPCODE,
  output ZERO,
  output NEGATIVE,
  output CARRY,
  output OVERFLOW,
  output [15:0] BUS_OUT
);

  wire addunit_1_sub_cout, addunit_1_sub_ovf, addunit_1_sum_cout, addunit_1_sum_ovf;
  wire [15:0] addunit_1_sub_16, addunit_1_sum_16, logicunit_1_logicand, logicunit_1_logicnot,
       logicunit_1_logicor, logicunit_1_logicxor, muxtree_1_result_internal, shiftunit_1_shl,
       shiftunit_1_shr, sltunit_1_lt;

  addunit addunit_1 (
    .A_16(A), .B_16(B), .SUM_16(addunit_1_sum_16), .SUM_COUT(addunit_1_sum_cout),
    .SUM_OVF(addunit_1_sum_ovf), .SUB_16(addunit_1_sub_16), .SUB_COUT(addunit_1_sub_cout),
    .SUB_OVF(addunit_1_sub_ovf));
  logicunit logicunit_1 (
    .A(A), .B(B), .logicAND(logicunit_1_logicand), .logicOR(logicunit_1_logicor),
    .logicXOR(logicunit_1_logicxor), .logicNOT(logicunit_1_logicnot));
  shiftunit shiftunit_1 (.A(A), .B(B), .shl(shiftunit_1_shl), .shr(shiftunit_1_shr));
  sltunit sltunit_1 (.A(A), .B(B), .LT(sltunit_1_lt));
  muxtree muxtree_1 (
    .op01001(addunit_1_sum_16), .op01010(addunit_1_sub_16), .op01101(logicunit_1_logicand),
    .op01110(logicunit_1_logicor), .op01111(logicunit_1_logicxor), .op10000(logicunit_1_logicnot),
    .op10001(shiftunit_1_shl), .op10010(shiftunit_1_shr), .op10011(sltunit_1_lt), .OPCODE(OPCODE),
    .RESULT_INTERNAL(muxtree_1_result_internal));  // open: op11011, op11100, op11101, op11110
  assign BUS_OUT = ALU_OUTPUT_ENABLE ? muxtree_1_result_internal : 16'bz;  // Controlled_Buffer controlled_buffer_1
  condition_logic condition_logic_1 (
    .SUM_COUT(addunit_1_sum_cout), .SUB_COUT(addunit_1_sub_cout), .SUM_OVF(addunit_1_sum_ovf),
    .SUB_OVF(addunit_1_sub_ovf), .RESULT_INTERNAL(muxtree_1_result_internal), .OPCODE(OPCODE), .ZERO(ZERO),
    .NEGATIVE(NEGATIVE), .CARRY(CARRY), .OVERFLOW(OVERFLOW));
endmodule

module tara_decoder (
  input  [15:0] IR,
  output [4:0] opcode,
  output [2:0] RD,
  output [2:0] RA,
  output [2:0] RB,
  output [7:0] IMM8,
  output [4:0] OFF5,
  output [7:0] REL8,
  output [10:0] REL11,
  output [2:0] Format
);

  wire comparator_1_gt, comparator_2_lt, comparator_3_gt, comparator_4_eq, comparator_5_eq, comparator_6_eq,
       comparator_7_eq, or_1_out;
  wire [2:0] multiplexer_1_out, multiplexer_2_out, multiplexer_5_out;

  Comparator #(.mode("unsigned"), .width(5)) comparator_1 (
    .a(5'b10111), .b(IR[15:11]), .gt(comparator_1_gt));  // open: eq, lt
  format_fun format_fun_1 (.opcode(IR[15:11]), .format(Format));
  Comparator #(.mode("unsigned"), .width(5)) comparator_2 (
    .a(5'b11000), .b(IR[15:11]), .lt(comparator_2_lt));  // open: gt, eq
  Multiplexer #(.width(3)) multiplexer_1 (.in0(3'b110), .in1(3'b111), .out(multiplexer_1_out), .sel(comparator_2_lt));
  Multiplexer #(.width(3)) multiplexer_2 (
    .in0(multiplexer_1_out), .in1(IR[10:8]), .out(multiplexer_2_out), .sel(comparator_1_gt));
  Comparator #(.mode("unsigned"), .width(3)) comparator_3 (
    .a(Format), .b(3'b010), .gt(comparator_3_gt));  // open: eq, lt
  Comparator #(.mode("unsigned"), .width(5)) comparator_4 (
    .a(IR[15:11]), .b(5'b11000), .eq(comparator_4_eq));  // open: gt, lt
  Comparator #(.mode("unsigned"), .width(3)) comparator_5 (
    .a(Format), .b(3'b100), .eq(comparator_5_eq));  // open: gt, lt
  Comparator #(.mode("unsigned"), .width(3)) comparator_6 (
    .a(Format), .b(3'b111), .eq(comparator_6_eq));  // open: gt, lt
  Multiplexer #(.width(3)) multiplexer_3 (.in0(IR[7:5]), .in1(multiplexer_2_out), .out(RA), .sel(or_1_out));
  or or_1 (or_1_out, comparator_3_gt, comparator_4_eq);
  Comparator #(.mode("unsigned"), .width(5)) comparator_7 (
    .a(5'b11010), .b(IR[15:11]), .eq(comparator_7_eq));  // open: gt, lt
  Multiplexer #(.width(3)) multiplexer_4 (.in0(multiplexer_2_out), .in1(IR[10:8]), .out(RD), .sel(comparator_7_eq));
  Multiplexer #(.width(3)) multiplexer_5 (.in0(IR[4:2]), .in1(IR[7:5]), .out(multiplexer_5_out), .sel(comparator_5_eq));
  Multiplexer #(.width(3)) multiplexer_6 (.in0(multiplexer_5_out), .in1(IR[10:8]), .out(RB), .sel(comparator_6_eq));

  assign IMM8 = IR[7:0];
  assign OFF5 = IR[4:0];
  assign opcode = IR[15:11];
  assign REL8 = IR[7:0];
  assign REL11 = IR[10:0];
endmodule

module format_fun (
  input  [4:0] opcode,
  output [2:0] format
);

  Multiplexer #(.select(5), .width(3)) multiplexer_1 (
    .in0(3'b000), .in1(3'b000), .in2(3'b010), .in3(3'b011), .in4(3'b011), .in5(3'b100), .in6(3'b100),
    .in7(3'b100), .in8(3'b100), .in9(3'b001), .in10(3'b001), .in11(3'b011), .in12(3'b001), .in13(3'b001),
    .in14(3'b001), .in15(3'b001), .in16(3'b010), .in17(3'b011), .in18(3'b011), .in19(3'b001), .in20(3'b101),
    .in21(3'b101), .in22(3'b110), .in23(3'b110), .in24(3'b000), .in25(3'b111), .in26(3'b111), .out(format),
    .sel(opcode));  // open: in27, in28, in29, in30, in31
endmodule

module D_latch (
  input  D,
  input  C,
  output Q,
  output Qinv
);

  wire nand_1_out, nand_2_out, not_1_out;

  not not_1 (not_1_out, D);
  nand nand_1 (nand_1_out, D, C);
  nand nand_2 (nand_2_out, C, not_1_out);
  nand nand_3 (Q, nand_1_out, Qinv);
  nand nand_4 (Qinv, Q, nand_2_out);

  // Notes on the sheet:
  //   CS25B031
  //   CS25B067
endmodule

module dff (
  input  D,
  input  CLK,
  input  EN,
  input  RST,
  output Q
);

  wire multiplexer_1_out;

  Multiplexer multiplexer_1 (.in0(Q), .in1(D), .out(multiplexer_1_out), .sel(EN));
  D_Flip_Flop d_ff_1 (.D(multiplexer_1_out), .clk(CLK), .Q(Q), .reset(RST));  // open: Qn, preset

  // Notes on the sheet:
  //   CS25B031
  //   CS25B067
endmodule

module half_adder (
  input  A,
  input  B,
  output SUM,
  output COUT
);

  xor xor_1 (SUM, A, B);
  and and_1 (COUT, B, A);
endmodule

module full_adder (
  input  A,
  input  B,
  input  CIN,
  output SUM,
  output COUT
);

  wire half_adder_1_cout, half_adder_1_sum, half_adder_2_cout;

  half_adder half_adder_1 (.A(A), .B(B), .SUM(half_adder_1_sum), .COUT(half_adder_1_cout));
  half_adder half_adder_2 (.A(half_adder_1_sum), .B(CIN), .SUM(SUM), .COUT(half_adder_2_cout));
  or or_1 (COUT, half_adder_1_cout, half_adder_2_cout);
endmodule

module adder16 (
  input  CIN,
  input  [15:0] A_16,
  input  [15:0] B_16,
  output [15:0] S_16,
  output COUT
);

  wire full_adder_1_cout, full_adder_2_cout, full_adder_3_cout, full_adder_4_cout, full_adder_5_cout,
       full_adder_6_cout, full_adder_7_cout, full_adder_8_cout, full_adder_9_cout, full_adder_10_cout,
       full_adder_11_cout, full_adder_12_cout, full_adder_13_cout, full_adder_14_cout, full_adder_15_cout;

  full_adder full_adder_1 (.A(A_16[0]), .B(B_16[0]), .CIN(CIN), .SUM(S_16[0]), .COUT(full_adder_1_cout));
  full_adder full_adder_2 (.A(A_16[1]), .B(B_16[1]), .CIN(full_adder_1_cout), .SUM(S_16[1]), .COUT(full_adder_2_cout));
  full_adder full_adder_3 (.A(A_16[2]), .B(B_16[2]), .CIN(full_adder_2_cout), .SUM(S_16[2]), .COUT(full_adder_3_cout));
  full_adder full_adder_4 (.A(A_16[3]), .B(B_16[3]), .CIN(full_adder_3_cout), .SUM(S_16[3]), .COUT(full_adder_4_cout));
  full_adder full_adder_5 (.A(A_16[4]), .B(B_16[4]), .CIN(full_adder_4_cout), .SUM(S_16[4]), .COUT(full_adder_5_cout));
  full_adder full_adder_6 (.A(A_16[5]), .B(B_16[5]), .CIN(full_adder_5_cout), .SUM(S_16[5]), .COUT(full_adder_6_cout));
  full_adder full_adder_7 (.A(A_16[6]), .B(B_16[6]), .CIN(full_adder_6_cout), .SUM(S_16[6]), .COUT(full_adder_7_cout));
  full_adder full_adder_8 (.A(A_16[7]), .B(B_16[7]), .CIN(full_adder_7_cout), .SUM(S_16[7]), .COUT(full_adder_8_cout));
  full_adder full_adder_9 (.A(A_16[8]), .B(B_16[8]), .CIN(full_adder_8_cout), .SUM(S_16[8]), .COUT(full_adder_9_cout));
  full_adder full_adder_10 (
    .A(A_16[9]), .B(B_16[9]), .CIN(full_adder_9_cout), .SUM(S_16[9]), .COUT(full_adder_10_cout));
  full_adder full_adder_11 (
    .A(A_16[10]), .B(B_16[10]), .CIN(full_adder_10_cout), .SUM(S_16[10]), .COUT(full_adder_11_cout));
  full_adder full_adder_12 (
    .A(A_16[11]), .B(B_16[11]), .CIN(full_adder_11_cout), .SUM(S_16[11]), .COUT(full_adder_12_cout));
  full_adder full_adder_13 (
    .A(A_16[12]), .B(B_16[12]), .CIN(full_adder_12_cout), .SUM(S_16[12]), .COUT(full_adder_13_cout));
  full_adder full_adder_14 (
    .A(A_16[13]), .B(B_16[13]), .CIN(full_adder_13_cout), .SUM(S_16[13]), .COUT(full_adder_14_cout));
  full_adder full_adder_15 (
    .A(A_16[14]), .B(B_16[14]), .CIN(full_adder_14_cout), .SUM(S_16[14]), .COUT(full_adder_15_cout));
  full_adder full_adder_16 (.A(A_16[15]), .B(B_16[15]), .CIN(full_adder_15_cout), .SUM(S_16[15]), .COUT(COUT));
endmodule

module addsub16 (
  input  SUB,
  input  [15:0] A_16,
  input  [15:0] B_16,
  output [15:0] S_16,
  output COUT,
  output OVF
);

  wire full_adder_1_cout, full_adder_2_cout, full_adder_3_cout, full_adder_4_cout, full_adder_5_cout,
       full_adder_6_cout, full_adder_7_cout, full_adder_8_cout, full_adder_9_cout, full_adder_10_cout,
       full_adder_11_cout, full_adder_12_cout, full_adder_13_cout, full_adder_14_cout, full_adder_15_cout;
  wire [15:0] multiplexer_1_out, not_1_out;

  Multiplexer #(.width(16)) multiplexer_1 (.in0(B_16), .in1(not_1_out), .out(multiplexer_1_out), .sel(SUB));
  assign not_1_out = ~B_16;  // NOT_Gate not_1, 16 bits wide
  full_adder full_adder_1 (.A(A_16[0]), .B(multiplexer_1_out[0]), .CIN(SUB), .SUM(S_16[0]), .COUT(full_adder_1_cout));
  full_adder full_adder_2 (
    .A(A_16[1]), .B(multiplexer_1_out[1]), .CIN(full_adder_1_cout), .SUM(S_16[1]), .COUT(full_adder_2_cout));
  full_adder full_adder_3 (
    .A(A_16[2]), .B(multiplexer_1_out[2]), .CIN(full_adder_2_cout), .SUM(S_16[2]), .COUT(full_adder_3_cout));
  full_adder full_adder_4 (
    .A(A_16[3]), .B(multiplexer_1_out[3]), .CIN(full_adder_3_cout), .SUM(S_16[3]), .COUT(full_adder_4_cout));
  full_adder full_adder_5 (
    .A(A_16[4]), .B(multiplexer_1_out[4]), .CIN(full_adder_4_cout), .SUM(S_16[4]), .COUT(full_adder_5_cout));
  full_adder full_adder_6 (
    .A(A_16[5]), .B(multiplexer_1_out[5]), .CIN(full_adder_5_cout), .SUM(S_16[5]), .COUT(full_adder_6_cout));
  full_adder full_adder_7 (
    .A(A_16[6]), .B(multiplexer_1_out[6]), .CIN(full_adder_6_cout), .SUM(S_16[6]), .COUT(full_adder_7_cout));
  full_adder full_adder_8 (
    .A(A_16[7]), .B(multiplexer_1_out[7]), .CIN(full_adder_7_cout), .SUM(S_16[7]), .COUT(full_adder_8_cout));
  full_adder full_adder_9 (
    .A(A_16[8]), .B(multiplexer_1_out[8]), .CIN(full_adder_8_cout), .SUM(S_16[8]), .COUT(full_adder_9_cout));
  full_adder full_adder_10 (
    .A(A_16[9]), .B(multiplexer_1_out[9]), .CIN(full_adder_9_cout), .SUM(S_16[9]), .COUT(full_adder_10_cout));
  full_adder full_adder_11 (
    .A(A_16[10]), .B(multiplexer_1_out[10]), .CIN(full_adder_10_cout), .SUM(S_16[10]),
    .COUT(full_adder_11_cout));
  full_adder full_adder_12 (
    .A(A_16[11]), .B(multiplexer_1_out[11]), .CIN(full_adder_11_cout), .SUM(S_16[11]),
    .COUT(full_adder_12_cout));
  full_adder full_adder_13 (
    .A(A_16[12]), .B(multiplexer_1_out[12]), .CIN(full_adder_12_cout), .SUM(S_16[12]),
    .COUT(full_adder_13_cout));
  full_adder full_adder_14 (
    .A(A_16[13]), .B(multiplexer_1_out[13]), .CIN(full_adder_13_cout), .SUM(S_16[13]),
    .COUT(full_adder_14_cout));
  full_adder full_adder_15 (
    .A(A_16[14]), .B(multiplexer_1_out[14]), .CIN(full_adder_14_cout), .SUM(S_16[14]),
    .COUT(full_adder_15_cout));
  full_adder full_adder_16 (
    .A(A_16[15]), .B(multiplexer_1_out[15]), .CIN(full_adder_15_cout), .SUM(S_16[15]), .COUT(COUT));
  xor xor_1 (OVF, COUT, full_adder_15_cout);
endmodule

module shl16 (
  input  [15:0] A_16,
  input  [4:0] SH_5,
  output [15:0] Y_16
);

  Multiplexer #(.select(5)) multiplexer_1 (
    .in0(A_16[0]), .in1(1'b0), .in2(1'b0), .in3(1'b0), .in4(1'b0), .in5(1'b0), .in6(1'b0), .in7(1'b0),
    .in8(1'b0), .in9(1'b0), .in10(1'b0), .in11(1'b0), .in12(1'b0), .in13(1'b0), .in14(1'b0), .in15(1'b0),
    .in16(1'b0), .in17(1'b0), .in18(1'b0), .in19(1'b0), .in20(1'b0), .in21(1'b0), .in22(1'b0), .in23(1'b0),
    .in24(1'b0), .in25(1'b0), .in26(1'b0), .in27(1'b0), .in28(1'b0), .in29(1'b0), .in30(1'b0), .in31(1'b0),
    .out(Y_16[0]), .sel(SH_5));
  Multiplexer #(.select(5)) multiplexer_2 (
    .in0(A_16[1]), .in1(A_16[0]), .in2(1'b0), .in3(1'b0), .in4(1'b0), .in5(1'b0), .in6(1'b0), .in7(1'b0),
    .in8(1'b0), .in9(1'b0), .in10(1'b0), .in11(1'b0), .in12(1'b0), .in13(1'b0), .in14(1'b0), .in15(1'b0),
    .in16(1'b0), .in17(1'b0), .in18(1'b0), .in19(1'b0), .in20(1'b0), .in21(1'b0), .in22(1'b0), .in23(1'b0),
    .in24(1'b0), .in25(1'b0), .in26(1'b0), .in27(1'b0), .in28(1'b0), .in29(1'b0), .in30(1'b0), .in31(1'b0),
    .out(Y_16[1]), .sel(SH_5));
  Multiplexer #(.select(5)) multiplexer_3 (
    .in0(A_16[2]), .in1(A_16[1]), .in2(A_16[0]), .in3(1'b0), .in4(1'b0), .in5(1'b0), .in6(1'b0), .in7(1'b0),
    .in8(1'b0), .in9(1'b0), .in10(1'b0), .in11(1'b0), .in12(1'b0), .in13(1'b0), .in14(1'b0), .in15(1'b0),
    .in16(1'b0), .in17(1'b0), .in18(1'b0), .in19(1'b0), .in20(1'b0), .in21(1'b0), .in22(1'b0), .in23(1'b0),
    .in24(1'b0), .in25(1'b0), .in26(1'b0), .in27(1'b0), .in28(1'b0), .in29(1'b0), .in30(1'b0), .in31(1'b0),
    .out(Y_16[2]), .sel(SH_5));
  Multiplexer #(.select(5)) multiplexer_4 (
    .in0(A_16[3]), .in1(A_16[2]), .in2(A_16[1]), .in3(A_16[0]), .in4(1'b0), .in5(1'b0), .in6(1'b0),
    .in7(1'b0), .in8(1'b0), .in9(1'b0), .in10(1'b0), .in11(1'b0), .in12(1'b0), .in13(1'b0), .in14(1'b0),
    .in15(1'b0), .in16(1'b0), .in17(1'b0), .in18(1'b0), .in19(1'b0), .in20(1'b0), .in21(1'b0), .in22(1'b0),
    .in23(1'b0), .in24(1'b0), .in25(1'b0), .in26(1'b0), .in27(1'b0), .in28(1'b0), .in29(1'b0), .in30(1'b0),
    .in31(1'b0), .out(Y_16[3]), .sel(SH_5));
  Multiplexer #(.select(5)) multiplexer_5 (
    .in0(A_16[4]), .in1(A_16[3]), .in2(A_16[2]), .in3(A_16[1]), .in4(A_16[0]), .in5(1'b0), .in6(1'b0),
    .in7(1'b0), .in8(1'b0), .in9(1'b0), .in10(1'b0), .in11(1'b0), .in12(1'b0), .in13(1'b0), .in14(1'b0),
    .in15(1'b0), .in16(1'b0), .in17(1'b0), .in18(1'b0), .in19(1'b0), .in20(1'b0), .in21(1'b0), .in22(1'b0),
    .in23(1'b0), .in24(1'b0), .in25(1'b0), .in26(1'b0), .in27(1'b0), .in28(1'b0), .in29(1'b0), .in30(1'b0),
    .in31(1'b0), .out(Y_16[4]), .sel(SH_5));
  Multiplexer #(.select(5)) multiplexer_6 (
    .in0(A_16[5]), .in1(A_16[4]), .in2(A_16[3]), .in3(A_16[2]), .in4(A_16[1]), .in5(A_16[0]), .in6(1'b0),
    .in7(1'b0), .in8(1'b0), .in9(1'b0), .in10(1'b0), .in11(1'b0), .in12(1'b0), .in13(1'b0), .in14(1'b0),
    .in15(1'b0), .in16(1'b0), .in17(1'b0), .in18(1'b0), .in19(1'b0), .in20(1'b0), .in21(1'b0), .in22(1'b0),
    .in23(1'b0), .in24(1'b0), .in25(1'b0), .in26(1'b0), .in27(1'b0), .in28(1'b0), .in29(1'b0), .in30(1'b0),
    .in31(1'b0), .out(Y_16[5]), .sel(SH_5));
  Multiplexer #(.select(5)) multiplexer_7 (
    .in0(A_16[6]), .in1(A_16[5]), .in2(A_16[4]), .in3(A_16[3]), .in4(A_16[2]), .in5(A_16[1]), .in6(A_16[0]),
    .in7(1'b0), .in8(1'b0), .in9(1'b0), .in10(1'b0), .in11(1'b0), .in12(1'b0), .in13(1'b0), .in14(1'b0),
    .in15(1'b0), .in16(1'b0), .in17(1'b0), .in18(1'b0), .in19(1'b0), .in20(1'b0), .in21(1'b0), .in22(1'b0),
    .in23(1'b0), .in24(1'b0), .in25(1'b0), .in26(1'b0), .in27(1'b0), .in28(1'b0), .in29(1'b0), .in30(1'b0),
    .in31(1'b0), .out(Y_16[6]), .sel(SH_5));
  Multiplexer #(.select(5)) multiplexer_8 (
    .in0(A_16[7]), .in1(A_16[6]), .in2(A_16[5]), .in3(A_16[4]), .in4(A_16[3]), .in5(A_16[2]), .in6(A_16[1]),
    .in7(A_16[0]), .in8(1'b0), .in9(1'b0), .in10(1'b0), .in11(1'b0), .in12(1'b0), .in13(1'b0), .in14(1'b0),
    .in15(1'b0), .in16(1'b0), .in17(1'b0), .in18(1'b0), .in19(1'b0), .in20(1'b0), .in21(1'b0), .in22(1'b0),
    .in23(1'b0), .in24(1'b0), .in25(1'b0), .in26(1'b0), .in27(1'b0), .in28(1'b0), .in29(1'b0), .in30(1'b0),
    .in31(1'b0), .out(Y_16[7]), .sel(SH_5));
  Multiplexer #(.select(5)) multiplexer_9 (
    .in0(A_16[8]), .in1(A_16[7]), .in2(A_16[6]), .in3(A_16[5]), .in4(A_16[4]), .in5(A_16[3]), .in6(A_16[2]),
    .in7(A_16[1]), .in8(A_16[0]), .in9(1'b0), .in10(1'b0), .in11(1'b0), .in12(1'b0), .in13(1'b0),
    .in14(1'b0), .in15(1'b0), .in16(1'b0), .in17(1'b0), .in18(1'b0), .in19(1'b0), .in20(1'b0), .in21(1'b0),
    .in22(1'b0), .in23(1'b0), .in24(1'b0), .in25(1'b0), .in26(1'b0), .in27(1'b0), .in28(1'b0), .in29(1'b0),
    .in30(1'b0), .in31(1'b0), .out(Y_16[8]), .sel(SH_5));
  Multiplexer #(.select(5)) multiplexer_10 (
    .in0(A_16[9]), .in1(A_16[8]), .in2(A_16[7]), .in3(A_16[6]), .in4(A_16[5]), .in5(A_16[4]), .in6(A_16[3]),
    .in7(A_16[2]), .in8(A_16[1]), .in9(A_16[0]), .in10(1'b0), .in11(1'b0), .in12(1'b0), .in13(1'b0),
    .in14(1'b0), .in15(1'b0), .in16(1'b0), .in17(1'b0), .in18(1'b0), .in19(1'b0), .in20(1'b0), .in21(1'b0),
    .in22(1'b0), .in23(1'b0), .in24(1'b0), .in25(1'b0), .in26(1'b0), .in27(1'b0), .in28(1'b0), .in29(1'b0),
    .in30(1'b0), .in31(1'b0), .out(Y_16[9]), .sel(SH_5));
  Multiplexer #(.select(5)) multiplexer_11 (
    .in0(A_16[10]), .in1(A_16[9]), .in2(A_16[8]), .in3(A_16[7]), .in4(A_16[6]), .in5(A_16[5]), .in6(A_16[4]),
    .in7(A_16[3]), .in8(A_16[2]), .in9(A_16[1]), .in10(A_16[0]), .in11(1'b0), .in12(1'b0), .in13(1'b0),
    .in14(1'b0), .in15(1'b0), .in16(1'b0), .in17(1'b0), .in18(1'b0), .in19(1'b0), .in20(1'b0), .in21(1'b0),
    .in22(1'b0), .in23(1'b0), .in24(1'b0), .in25(1'b0), .in26(1'b0), .in27(1'b0), .in28(1'b0), .in29(1'b0),
    .in30(1'b0), .in31(1'b0), .out(Y_16[10]), .sel(SH_5));
  Multiplexer #(.select(5)) multiplexer_12 (
    .in0(A_16[11]), .in1(A_16[10]), .in2(A_16[9]), .in3(A_16[8]), .in4(A_16[7]), .in5(A_16[6]),
    .in6(A_16[5]), .in7(A_16[4]), .in8(A_16[3]), .in9(A_16[2]), .in10(A_16[1]), .in11(A_16[0]), .in12(1'b0),
    .in13(1'b0), .in14(1'b0), .in15(1'b0), .in16(1'b0), .in17(1'b0), .in18(1'b0), .in19(1'b0), .in20(1'b0),
    .in21(1'b0), .in22(1'b0), .in23(1'b0), .in24(1'b0), .in25(1'b0), .in26(1'b0), .in27(1'b0), .in28(1'b0),
    .in29(1'b0), .in30(1'b0), .in31(1'b0), .out(Y_16[11]), .sel(SH_5));
  Multiplexer #(.select(5)) multiplexer_13 (
    .in0(A_16[12]), .in1(A_16[11]), .in2(A_16[10]), .in3(A_16[9]), .in4(A_16[8]), .in5(A_16[7]),
    .in6(A_16[6]), .in7(A_16[5]), .in8(A_16[4]), .in9(A_16[3]), .in10(A_16[2]), .in11(A_16[1]),
    .in12(A_16[0]), .in13(1'b0), .in14(1'b0), .in15(1'b0), .in16(1'b0), .in17(1'b0), .in18(1'b0),
    .in19(1'b0), .in20(1'b0), .in21(1'b0), .in22(1'b0), .in23(1'b0), .in24(1'b0), .in25(1'b0), .in26(1'b0),
    .in27(1'b0), .in28(1'b0), .in29(1'b0), .in30(1'b0), .in31(1'b0), .out(Y_16[12]), .sel(SH_5));
  Multiplexer #(.select(5)) multiplexer_14 (
    .in0(A_16[13]), .in1(A_16[12]), .in2(A_16[11]), .in3(A_16[10]), .in4(A_16[9]), .in5(A_16[8]),
    .in6(A_16[7]), .in7(A_16[6]), .in8(A_16[5]), .in9(A_16[4]), .in10(A_16[3]), .in11(A_16[2]),
    .in12(A_16[1]), .in13(A_16[0]), .in14(1'b0), .in15(1'b0), .in16(1'b0), .in17(1'b0), .in18(1'b0),
    .in19(1'b0), .in20(1'b0), .in21(1'b0), .in22(1'b0), .in23(1'b0), .in24(1'b0), .in25(1'b0), .in26(1'b0),
    .in27(1'b0), .in28(1'b0), .in29(1'b0), .in30(1'b0), .in31(1'b0), .out(Y_16[13]), .sel(SH_5));
  Multiplexer #(.select(5)) multiplexer_15 (
    .in0(A_16[14]), .in1(A_16[13]), .in2(A_16[12]), .in3(A_16[11]), .in4(A_16[10]), .in5(A_16[9]),
    .in6(A_16[8]), .in7(A_16[7]), .in8(A_16[6]), .in9(A_16[5]), .in10(A_16[4]), .in11(A_16[3]),
    .in12(A_16[2]), .in13(A_16[1]), .in14(A_16[0]), .in15(1'b0), .in16(1'b0), .in17(1'b0), .in18(1'b0),
    .in19(1'b0), .in20(1'b0), .in21(1'b0), .in22(1'b0), .in23(1'b0), .in24(1'b0), .in25(1'b0), .in26(1'b0),
    .in27(1'b0), .in28(1'b0), .in29(1'b0), .in30(1'b0), .in31(1'b0), .out(Y_16[14]), .sel(SH_5));
  Multiplexer #(.select(5)) multiplexer_16 (
    .in0(A_16[15]), .in1(A_16[14]), .in2(A_16[13]), .in3(A_16[12]), .in4(A_16[11]), .in5(A_16[10]),
    .in6(A_16[9]), .in7(A_16[8]), .in8(A_16[7]), .in9(A_16[6]), .in10(A_16[5]), .in11(A_16[4]),
    .in12(A_16[3]), .in13(A_16[2]), .in14(A_16[1]), .in15(A_16[0]), .in16(1'b0), .in17(1'b0), .in18(1'b0),
    .in19(1'b0), .in20(1'b0), .in21(1'b0), .in22(1'b0), .in23(1'b0), .in24(1'b0), .in25(1'b0), .in26(1'b0),
    .in27(1'b0), .in28(1'b0), .in29(1'b0), .in30(1'b0), .in31(1'b0), .out(Y_16[15]), .sel(SH_5));
endmodule

module cmp4 (
  input  [3:0] A,
  input  [3:0] B,
  input  EQin,
  input  LTin,
  input  GTin,
  output EQ,
  output LT,
  output GT
);

  wire and_1_out, and_2_out, and_3_out, and_4_out, and_5_out, and_6_out, and_7_out, and_8_out, and_10_out,
       and_11_out, and_12_out, not_1_out, not_2_out, not_3_out, not_4_out, not_5_out, not_6_out, not_7_out,
       not_8_out, not_9_out, not_10_out, or_1_out, xor_1_out, xor_2_out, xor_3_out, xor_4_out;

  xor xor_1 (xor_1_out, B[0], A[0]);
  xor xor_2 (xor_2_out, B[1], A[1]);
  xor xor_3 (xor_3_out, B[2], A[2]);
  xor xor_4 (xor_4_out, B[3], A[3]);
  not not_1 (not_1_out, xor_1_out);
  not not_2 (not_2_out, xor_2_out);
  not not_3 (not_3_out, xor_3_out);
  not not_4 (not_4_out, xor_4_out);
  not not_5 (not_5_out, B[0]);
  not not_6 (not_6_out, B[1]);
  not not_7 (not_7_out, B[2]);
  not not_8 (not_8_out, B[3]);
  and and_1 (and_1_out, not_5_out, A[0]);
  and and_2 (and_2_out, not_6_out, A[1]);
  and and_3 (and_3_out, not_7_out, A[2]);
  and and_4 (and_4_out, not_8_out, A[3]);
  and and_5 (and_5_out, not_1_out, not_2_out, not_3_out, not_4_out);
  not not_9 (not_9_out, and_5_out);
  and and_6 (and_6_out, and_1_out, not_2_out, not_3_out, not_4_out);
  and and_7 (and_7_out, and_2_out, not_3_out, not_4_out);
  and and_8 (and_8_out, and_3_out, not_4_out);
  and and_9 (EQ, EQin, and_5_out);
  or or_1 (or_1_out, and_6_out, and_7_out, and_8_out, and_4_out);
  and and_10 (and_10_out, GTin, and_5_out);
  and and_11 (and_11_out, not_10_out, not_9_out);
  not not_10 (not_10_out, or_1_out);
  and and_12 (and_12_out, LTin, and_5_out);
  or or_2 (LT, and_12_out, and_11_out);
  or or_3 (GT, and_10_out, or_1_out);
endmodule

module cmp16 (
  input  [15:0] A_16,
  input  [15:0] B_16,
  output EQ,
  output LT,
  output GT
);

  wire cmp4_1_eq, cmp4_1_gt, cmp4_1_lt, cmp4_2_eq, cmp4_2_gt, cmp4_2_lt, cmp4_3_eq, cmp4_3_gt, cmp4_3_lt;

  cmp4 cmp4_1 (
    .A(A_16[3:0]), .B(B_16[3:0]), .EQin(1'b1), .LTin(1'b0), .GTin(1'b0), .EQ(cmp4_1_eq), .LT(cmp4_1_lt),
    .GT(cmp4_1_gt));
  cmp4 cmp4_2 (
    .A(A_16[7:4]), .B(B_16[7:4]), .EQin(cmp4_1_eq), .LTin(cmp4_1_lt), .GTin(cmp4_1_gt), .EQ(cmp4_2_eq),
    .LT(cmp4_2_lt), .GT(cmp4_2_gt));
  cmp4 cmp4_3 (
    .A(A_16[11:8]), .B(B_16[11:8]), .EQin(cmp4_2_eq), .LTin(cmp4_2_lt), .GTin(cmp4_2_gt), .EQ(cmp4_3_eq),
    .LT(cmp4_3_lt), .GT(cmp4_3_gt));
  cmp4 cmp4_4 (
    .A(A_16[15:12]), .B(B_16[15:12]), .EQin(cmp4_3_eq), .LTin(cmp4_3_lt), .GTin(cmp4_3_gt), .EQ(EQ), .LT(LT),
    .GT(GT));
endmodule

module shr16 (
  input  [15:0] A_16,
  input  [4:0] SH_5,
  output [15:0] Y_16
);

  Multiplexer #(.select(5)) multiplexer_1 (
    .in0(A_16[15]), .in1(1'b0), .in2(1'b0), .in3(1'b0), .in4(1'b0), .in5(1'b0), .in6(1'b0), .in7(1'b0),
    .in8(1'b0), .in9(1'b0), .in10(1'b0), .in11(1'b0), .in12(1'b0), .in13(1'b0), .in14(1'b0), .in15(1'b0),
    .in16(1'b0), .in17(1'b0), .in18(1'b0), .in19(1'b0), .in20(1'b0), .in21(1'b0), .in22(1'b0), .in23(1'b0),
    .in24(1'b0), .in25(1'b0), .in26(1'b0), .in27(1'b0), .in28(1'b0), .in29(1'b0), .in30(1'b0), .in31(1'b0),
    .out(Y_16[15]), .sel(SH_5));
  Multiplexer #(.select(5)) multiplexer_2 (
    .in0(A_16[14]), .in1(A_16[15]), .in2(1'b0), .in3(1'b0), .in4(1'b0), .in5(1'b0), .in6(1'b0), .in7(1'b0),
    .in8(1'b0), .in9(1'b0), .in10(1'b0), .in11(1'b0), .in12(1'b0), .in13(1'b0), .in14(1'b0), .in15(1'b0),
    .in16(1'b0), .in17(1'b0), .in18(1'b0), .in19(1'b0), .in20(1'b0), .in21(1'b0), .in22(1'b0), .in23(1'b0),
    .in24(1'b0), .in25(1'b0), .in26(1'b0), .in27(1'b0), .in28(1'b0), .in29(1'b0), .in30(1'b0), .in31(1'b0),
    .out(Y_16[14]), .sel(SH_5));
  Multiplexer #(.select(5)) multiplexer_3 (
    .in0(A_16[13]), .in1(A_16[14]), .in2(A_16[15]), .in3(1'b0), .in4(1'b0), .in5(1'b0), .in6(1'b0),
    .in7(1'b0), .in8(1'b0), .in9(1'b0), .in10(1'b0), .in11(1'b0), .in12(1'b0), .in13(1'b0), .in14(1'b0),
    .in15(1'b0), .in16(1'b0), .in17(1'b0), .in18(1'b0), .in19(1'b0), .in20(1'b0), .in21(1'b0), .in22(1'b0),
    .in23(1'b0), .in24(1'b0), .in25(1'b0), .in26(1'b0), .in27(1'b0), .in28(1'b0), .in29(1'b0), .in30(1'b0),
    .in31(1'b0), .out(Y_16[13]), .sel(SH_5));
  Multiplexer #(.select(5)) multiplexer_4 (
    .in0(A_16[12]), .in1(A_16[13]), .in2(A_16[14]), .in3(A_16[15]), .in4(1'b0), .in5(1'b0), .in6(1'b0),
    .in7(1'b0), .in8(1'b0), .in9(1'b0), .in10(1'b0), .in11(1'b0), .in12(1'b0), .in13(1'b0), .in14(1'b0),
    .in15(1'b0), .in16(1'b0), .in17(1'b0), .in18(1'b0), .in19(1'b0), .in20(1'b0), .in21(1'b0), .in22(1'b0),
    .in23(1'b0), .in24(1'b0), .in25(1'b0), .in26(1'b0), .in27(1'b0), .in28(1'b0), .in29(1'b0), .in30(1'b0),
    .in31(1'b0), .out(Y_16[12]), .sel(SH_5));
  Multiplexer #(.select(5)) multiplexer_5 (
    .in0(A_16[11]), .in1(A_16[12]), .in2(A_16[13]), .in3(A_16[14]), .in4(A_16[15]), .in5(1'b0), .in6(1'b0),
    .in7(1'b0), .in8(1'b0), .in9(1'b0), .in10(1'b0), .in11(1'b0), .in12(1'b0), .in13(1'b0), .in14(1'b0),
    .in15(1'b0), .in16(1'b0), .in17(1'b0), .in18(1'b0), .in19(1'b0), .in20(1'b0), .in21(1'b0), .in22(1'b0),
    .in23(1'b0), .in24(1'b0), .in25(1'b0), .in26(1'b0), .in27(1'b0), .in28(1'b0), .in29(1'b0), .in30(1'b0),
    .in31(1'b0), .out(Y_16[11]), .sel(SH_5));
  Multiplexer #(.select(5)) multiplexer_6 (
    .in0(A_16[10]), .in1(A_16[11]), .in2(A_16[12]), .in3(A_16[13]), .in4(A_16[14]), .in5(A_16[15]),
    .in6(1'b0), .in7(1'b0), .in8(1'b0), .in9(1'b0), .in10(1'b0), .in11(1'b0), .in12(1'b0), .in13(1'b0),
    .in14(1'b0), .in15(1'b0), .in16(1'b0), .in17(1'b0), .in18(1'b0), .in19(1'b0), .in20(1'b0), .in21(1'b0),
    .in22(1'b0), .in23(1'b0), .in24(1'b0), .in25(1'b0), .in26(1'b0), .in27(1'b0), .in28(1'b0), .in29(1'b0),
    .in30(1'b0), .in31(1'b0), .out(Y_16[10]), .sel(SH_5));
  Multiplexer #(.select(5)) multiplexer_7 (
    .in0(A_16[9]), .in1(A_16[10]), .in2(A_16[11]), .in3(A_16[12]), .in4(A_16[13]), .in5(A_16[14]),
    .in6(A_16[15]), .in7(1'b0), .in8(1'b0), .in9(1'b0), .in10(1'b0), .in11(1'b0), .in12(1'b0), .in13(1'b0),
    .in14(1'b0), .in15(1'b0), .in16(1'b0), .in17(1'b0), .in18(1'b0), .in19(1'b0), .in20(1'b0), .in21(1'b0),
    .in22(1'b0), .in23(1'b0), .in24(1'b0), .in25(1'b0), .in26(1'b0), .in27(1'b0), .in28(1'b0), .in29(1'b0),
    .in30(1'b0), .in31(1'b0), .out(Y_16[9]), .sel(SH_5));
  Multiplexer #(.select(5)) multiplexer_8 (
    .in0(A_16[8]), .in1(A_16[9]), .in2(A_16[10]), .in3(A_16[11]), .in4(A_16[12]), .in5(A_16[13]),
    .in6(A_16[14]), .in7(A_16[15]), .in8(1'b0), .in9(1'b0), .in10(1'b0), .in11(1'b0), .in12(1'b0),
    .in13(1'b0), .in14(1'b0), .in15(1'b0), .in16(1'b0), .in17(1'b0), .in18(1'b0), .in19(1'b0), .in20(1'b0),
    .in21(1'b0), .in22(1'b0), .in23(1'b0), .in24(1'b0), .in25(1'b0), .in26(1'b0), .in27(1'b0), .in28(1'b0),
    .in29(1'b0), .in30(1'b0), .in31(1'b0), .out(Y_16[8]), .sel(SH_5));
  Multiplexer #(.select(5)) multiplexer_9 (
    .in0(A_16[7]), .in1(A_16[8]), .in2(A_16[9]), .in3(A_16[10]), .in4(A_16[11]), .in5(A_16[12]),
    .in6(A_16[13]), .in7(A_16[14]), .in8(A_16[15]), .in9(1'b0), .in10(1'b0), .in11(1'b0), .in12(1'b0),
    .in13(1'b0), .in14(1'b0), .in15(1'b0), .in16(1'b0), .in17(1'b0), .in18(1'b0), .in19(1'b0), .in20(1'b0),
    .in21(1'b0), .in22(1'b0), .in23(1'b0), .in24(1'b0), .in25(1'b0), .in26(1'b0), .in27(1'b0), .in28(1'b0),
    .in29(1'b0), .in30(1'b0), .in31(1'b0), .out(Y_16[7]), .sel(SH_5));
  Multiplexer #(.select(5)) multiplexer_10 (
    .in0(A_16[6]), .in1(A_16[7]), .in2(A_16[8]), .in3(A_16[9]), .in4(A_16[10]), .in5(A_16[11]),
    .in6(A_16[12]), .in7(A_16[13]), .in8(A_16[14]), .in9(A_16[15]), .in10(1'b0), .in11(1'b0), .in12(1'b0),
    .in13(1'b0), .in14(1'b0), .in15(1'b0), .in16(1'b0), .in17(1'b0), .in18(1'b0), .in19(1'b0), .in20(1'b0),
    .in21(1'b0), .in22(1'b0), .in23(1'b0), .in24(1'b0), .in25(1'b0), .in26(1'b0), .in27(1'b0), .in28(1'b0),
    .in29(1'b0), .in30(1'b0), .in31(1'b0), .out(Y_16[6]), .sel(SH_5));
  Multiplexer #(.select(5)) multiplexer_11 (
    .in0(A_16[5]), .in1(A_16[6]), .in2(A_16[7]), .in3(A_16[8]), .in4(A_16[9]), .in5(A_16[10]),
    .in6(A_16[11]), .in7(A_16[12]), .in8(A_16[13]), .in9(A_16[14]), .in10(A_16[15]), .in11(1'b0),
    .in12(1'b0), .in13(1'b0), .in14(1'b0), .in15(1'b0), .in16(1'b0), .in17(1'b0), .in18(1'b0), .in19(1'b0),
    .in20(1'b0), .in21(1'b0), .in22(1'b0), .in23(1'b0), .in24(1'b0), .in25(1'b0), .in26(1'b0), .in27(1'b0),
    .in28(1'b0), .in29(1'b0), .in30(1'b0), .in31(1'b0), .out(Y_16[5]), .sel(SH_5));
  Multiplexer #(.select(5)) multiplexer_12 (
    .in0(A_16[4]), .in1(A_16[5]), .in2(A_16[6]), .in3(A_16[7]), .in4(A_16[8]), .in5(A_16[9]), .in6(A_16[10]),
    .in7(A_16[11]), .in8(A_16[12]), .in9(A_16[13]), .in10(A_16[14]), .in11(A_16[15]), .in12(1'b0),
    .in13(1'b0), .in14(1'b0), .in15(1'b0), .in16(1'b0), .in17(1'b0), .in18(1'b0), .in19(1'b0), .in20(1'b0),
    .in21(1'b0), .in22(1'b0), .in23(1'b0), .in24(1'b0), .in25(1'b0), .in26(1'b0), .in27(1'b0), .in28(1'b0),
    .in29(1'b0), .in30(1'b0), .in31(1'b0), .out(Y_16[4]), .sel(SH_5));
  Multiplexer #(.select(5)) multiplexer_13 (
    .in0(A_16[3]), .in1(A_16[4]), .in2(A_16[5]), .in3(A_16[6]), .in4(A_16[7]), .in5(A_16[8]), .in6(A_16[9]),
    .in7(A_16[10]), .in8(A_16[11]), .in9(A_16[12]), .in10(A_16[13]), .in11(A_16[14]), .in12(A_16[15]),
    .in13(1'b0), .in14(1'b0), .in15(1'b0), .in16(1'b0), .in17(1'b0), .in18(1'b0), .in19(1'b0), .in20(1'b0),
    .in21(1'b0), .in22(1'b0), .in23(1'b0), .in24(1'b0), .in25(1'b0), .in26(1'b0), .in27(1'b0), .in28(1'b0),
    .in29(1'b0), .in30(1'b0), .in31(1'b0), .out(Y_16[3]), .sel(SH_5));
  Multiplexer #(.select(5)) multiplexer_14 (
    .in0(A_16[2]), .in1(A_16[3]), .in2(A_16[4]), .in3(A_16[5]), .in4(A_16[6]), .in5(A_16[7]), .in6(A_16[8]),
    .in7(A_16[9]), .in8(A_16[10]), .in9(A_16[11]), .in10(A_16[12]), .in11(A_16[13]), .in12(A_16[14]),
    .in13(A_16[15]), .in14(1'b0), .in15(1'b0), .in16(1'b0), .in17(1'b0), .in18(1'b0), .in19(1'b0),
    .in20(1'b0), .in21(1'b0), .in22(1'b0), .in23(1'b0), .in24(1'b0), .in25(1'b0), .in26(1'b0), .in27(1'b0),
    .in28(1'b0), .in29(1'b0), .in30(1'b0), .in31(1'b0), .out(Y_16[2]), .sel(SH_5));
  Multiplexer #(.select(5)) multiplexer_15 (
    .in0(A_16[1]), .in1(A_16[2]), .in2(A_16[3]), .in3(A_16[4]), .in4(A_16[5]), .in5(A_16[6]), .in6(A_16[7]),
    .in7(A_16[8]), .in8(A_16[9]), .in9(A_16[10]), .in10(A_16[11]), .in11(A_16[12]), .in12(A_16[13]),
    .in13(A_16[14]), .in14(A_16[15]), .in15(1'b0), .in16(1'b0), .in17(1'b0), .in18(1'b0), .in19(1'b0),
    .in20(1'b0), .in21(1'b0), .in22(1'b0), .in23(1'b0), .in24(1'b0), .in25(1'b0), .in26(1'b0), .in27(1'b0),
    .in28(1'b0), .in29(1'b0), .in30(1'b0), .in31(1'b0), .out(Y_16[1]), .sel(SH_5));
  Multiplexer #(.select(5)) multiplexer_16 (
    .in0(A_16[0]), .in1(A_16[1]), .in2(A_16[2]), .in3(A_16[3]), .in4(A_16[4]), .in5(A_16[5]), .in6(A_16[6]),
    .in7(A_16[7]), .in8(A_16[8]), .in9(A_16[9]), .in10(A_16[10]), .in11(A_16[11]), .in12(A_16[12]),
    .in13(A_16[13]), .in14(A_16[14]), .in15(A_16[15]), .in16(1'b0), .in17(1'b0), .in18(1'b0), .in19(1'b0),
    .in20(1'b0), .in21(1'b0), .in22(1'b0), .in23(1'b0), .in24(1'b0), .in25(1'b0), .in26(1'b0), .in27(1'b0),
    .in28(1'b0), .in29(1'b0), .in30(1'b0), .in31(1'b0), .out(Y_16[0]), .sel(SH_5));
endmodule

module sltunit (
  input  [15:0] A,
  input  [15:0] B,
  output [15:0] LT
);

  wire and_1_out, and_2_out, cmp16_1_lt, not_1_out, not_2_out, xor_1_out;

  not not_1 (not_1_out, B[15]);
  and and_1 (and_1_out, A[15], not_1_out);
  cmp16 cmp16_1 (.A_16(A), .B_16(B), .LT(cmp16_1_lt));  // open: EQ, GT
  xor xor_1 (xor_1_out, A[15], B[15]);
  not not_2 (not_2_out, xor_1_out);
  and and_2 (and_2_out, not_2_out, cmp16_1_lt);
  or or_1 (LT[0], and_1_out, and_2_out);

  assign LT[15:1] = {15{1'b0}};
endmodule

module addunit (
  input  [15:0] A_16,
  input  [15:0] B_16,
  output [15:0] SUM_16,
  output SUM_COUT,
  output SUM_OVF,
  output [15:0] SUB_16,
  output SUB_COUT,
  output SUB_OVF
);

  wire not_1_out;

  not not_1 (not_1_out, 1'b0);
  addsub16 addsub16_1 (.SUB(1'b0), .A_16(A_16), .B_16(B_16), .S_16(SUM_16), .COUT(SUM_COUT), .OVF(SUM_OVF));
  addsub16 addsub16_2 (.SUB(not_1_out), .A_16(A_16), .B_16(B_16), .S_16(SUB_16), .COUT(SUB_COUT), .OVF(SUB_OVF));
endmodule

module logicunit (
  input  [15:0] A,
  input  [15:0] B,
  output [15:0] logicAND,
  output [15:0] logicOR,
  output [15:0] logicXOR,
  output [15:0] logicNOT
);

  assign logicAND = A & B;  // AND_Gate and_1, 16 bits wide
  assign logicOR = A | B;  // OR_Gate or_1, 16 bits wide
  assign logicXOR = A ^ B;  // XOR_Gate xor_1, 16 bits wide
  assign logicNOT = ~A;  // NOT_Gate not_1, 16 bits wide
endmodule

module shiftunit (
  input  [15:0] A,
  input  [15:0] B,
  output [15:0] shl,
  output [15:0] shr
);

  shl16 shl16_1 (.A_16(A), .SH_5(B[4:0]), .Y_16(shl));
  shr16 shr16_1 (.A_16(A), .SH_5(B[4:0]), .Y_16(shr));
endmodule

module muxtree (
  input  [15:0] op01001,
  input  [15:0] op01010,
  input  [15:0] op01101,
  input  [15:0] op01110,
  input  [15:0] op01111,
  input  [15:0] op10000,
  input  [15:0] op10001,
  input  [15:0] op10010,
  input  [15:0] op10011,
  input  [15:0] op11011,
  input  [15:0] op11100,
  input  [15:0] op11101,
  input  [15:0] op11110,
  input  [4:0] OPCODE,
  output [15:0] RESULT_INTERNAL
);

  wire [15:0] multiplexer_1_out, multiplexer_2_out, multiplexer_3_out, multiplexer_4_out, multiplexer_5_out,
       multiplexer_6_out, multiplexer_7_out, multiplexer_8_out, multiplexer_9_out, multiplexer_10_out,
       multiplexer_12_out;

  Multiplexer #(.width(16)) multiplexer_1 (.in0(op11100), .in1(op11101), .out(multiplexer_1_out), .sel(OPCODE[0]));
  Multiplexer #(.width(16)) multiplexer_2 (.in0(op10000), .in1(op10001), .out(multiplexer_2_out), .sel(OPCODE[0]));
  Multiplexer #(.width(16)) multiplexer_3 (.in0(op10010), .in1(op10011), .out(multiplexer_3_out), .sel(OPCODE[0]));
  Multiplexer #(.width(16)) multiplexer_4 (
    .in0(multiplexer_1_out), .in1(op11110), .out(multiplexer_4_out), .sel(OPCODE[1]));
  Multiplexer #(.width(16)) multiplexer_5 (.in0(op01001), .in1(op01010), .out(multiplexer_5_out), .sel(OPCODE[1]));
  Multiplexer #(.width(16)) multiplexer_6 (
    .in0(op01101), .in1(multiplexer_7_out), .out(multiplexer_6_out), .sel(OPCODE[1]));
  Multiplexer #(.width(16)) multiplexer_7 (.in0(op01110), .in1(op01111), .out(multiplexer_7_out), .sel(OPCODE[0]));
  Multiplexer #(.width(16)) multiplexer_8 (
    .in0(op11011), .in1(multiplexer_4_out), .out(multiplexer_8_out), .sel(OPCODE[2]));
  Multiplexer #(.width(16)) multiplexer_9 (
    .in0(multiplexer_5_out), .in1(multiplexer_6_out), .out(multiplexer_9_out), .sel(OPCODE[2]));
  Multiplexer #(.width(16)) multiplexer_10 (
    .in0(multiplexer_2_out), .in1(multiplexer_3_out), .out(multiplexer_10_out), .sel(OPCODE[1]));
  Multiplexer #(.width(16)) multiplexer_11 (
    .in0(multiplexer_9_out), .in1(multiplexer_12_out), .out(RESULT_INTERNAL), .sel(OPCODE[4]));
  Multiplexer #(.width(16)) multiplexer_12 (
    .in0(multiplexer_10_out), .in1(multiplexer_8_out), .out(multiplexer_12_out), .sel(OPCODE[3]));
endmodule

module condition_logic (
  input  SUM_COUT,
  input  SUB_COUT,
  input  SUM_OVF,
  input  SUB_OVF,
  input  [15:0] RESULT_INTERNAL,
  input  [4:0] OPCODE,
  output ZERO,
  output NEGATIVE,
  output CARRY,
  output OVERFLOW
);

  wire and_1_out, multiplexer_1_out, multiplexer_2_out, not_2_out, not_3_out, or_1_out;

  or or_1 (or_1_out, RESULT_INTERNAL[0], RESULT_INTERNAL[1], RESULT_INTERNAL[2], RESULT_INTERNAL[3], RESULT_INTERNAL[4], RESULT_INTERNAL[5], RESULT_INTERNAL[6], RESULT_INTERNAL[7], RESULT_INTERNAL[8], RESULT_INTERNAL[9], RESULT_INTERNAL[10], RESULT_INTERNAL[11], RESULT_INTERNAL[12], RESULT_INTERNAL[13], RESULT_INTERNAL[14], RESULT_INTERNAL[15]);
  not not_1 (ZERO, or_1_out);
  Multiplexer multiplexer_1 (.in0(SUM_COUT), .in1(SUB_COUT), .out(multiplexer_1_out), .sel(OPCODE[1]));
  Multiplexer multiplexer_2 (.in0(SUM_OVF), .in1(SUB_OVF), .out(multiplexer_2_out), .sel(OPCODE[1]));
  not not_2 (not_2_out, OPCODE[4]);
  not not_3 (not_3_out, OPCODE[2]);
  and and_1 (and_1_out, not_2_out, OPCODE[3], not_3_out);
  and and_2 (CARRY, multiplexer_1_out, and_1_out);
  and and_3 (OVERFLOW, multiplexer_2_out, and_1_out);

  assign NEGATIVE = RESULT_INTERNAL[15];
endmodule

module T_Counter (
  input  CLK,
  input  Step_Reset,
  input  HLT,
  input  Reset,
  output [3:0] Tstate
);

  wire not_1_out;
  wire [3:0] adder_1_out, multiplexer_1_out;

  not not_1 (not_1_out, HLT);
  Multiplexer #(.width(4)) multiplexer_1 (.in0(adder_1_out), .in1(4'b0000), .out(multiplexer_1_out), .sel(Step_Reset));
  Register #(.width(4)) register_1 (.D(multiplexer_1_out), .en(not_1_out), .clk(CLK), .Q(Tstate), .clr(Reset));
  Adder #(.width(4)) adder_1 (.a(Tstate), .b(4'b0001), .out(adder_1_out));  // open: cin, cout
endmodule

module Control_ROM (
  input  Z,
  input  N,
  input  CLK,
  input  [4:0] OPCODE,
  input  RST,
  output [4:0] ALU_select,
  output PC_load,
  output PC_inc,
  output PC_add,
  output MAR_load,
  output MDR_select,
  output MDR_load,
  output IR_load,
  output Regfile_load,
  output Alu_out,
  output Status_load,
  output Mem_read,
  output Mem_write,
  output clock,
  output reset,
  output [3:0] Bus_source
);

  wire [3:0] t_counter_1_tstate;
  wire [6:5] rom_1_data;

  T_Counter t_counter_1 (
    .CLK(CLK), .Step_Reset(rom_1_data[6]), .HLT(rom_1_data[5]), .Reset(RST), .Tstate(t_counter_1_tstate));
  ROM #(.addrWidth(11), .dataWidth(23)) rom_1 (
    .addr({Z, N, OPCODE, t_counter_1_tstate}),
    .data({Bus_source, PC_load, PC_inc, PC_add, MAR_load, MDR_select, MDR_load, IR_load, Alu_out, Regfile_load, Mem_read, Mem_write, Status_load, rom_1_data, ALU_select}));

  assign clock = CLK;
  assign reset = RST;

  // Notes on the sheet:
  //   contents of rom_1 (hex, n*v repeats v):
  //   8000 6200 81000 60040 12*40 8000 6200 81000 20 12*40 8000 6200 81000 180400 60040 11*40 8000 6200
  //   81000 200400 60040 11*40 8000 6200 81000 480400 60040 11*40 8000 6200 81000 400809 408800 86200
  //   80400 60040 8*40 8000 6200 81000 400809 408800 182000 80100 60040 8*40 8000 6200 81000 400809 408800
  //   86200 80400 60040 8*40 8000 6200 81000 400809 408800 182000 80100 60040 8*40 8000 6200 81000 400889
  //   400c00 60040 10*40 8000 6200 81000 40088a 400c00 60040 10*40 8000 6200 81000 400889 400c00 60040
  //   10*40 8000 6200 81000 13*40 8000 6200 81000 40088d 400c00 60040 10*40 8000 6200 81000 40088e 400c00
  //   60040 10*40 8000 6200 81000 40088f 400c00 60040 10*40 8000 6200 81000 400890 400c00 60040 10*40 8000
  //   6200 81000 400891 400c00 60040 10*40 8000 6200 81000 400892 400c00 60040 10*40 8000 6200 81000
  //   400893 400c00 60040 10*40 8000 6200 81000 400809 60000 11*40 8000 6200 81000 400809 60000 11*40 8000
  //   6200 81000 70000 60040 11*40 8000 6200 81000 400 470809 400c00 60040 9*40 8000 6200 81000 1c0000
  //   12*40 8000 6200 81000 40080a 400c00 188000 2000 80100 60040 7*40 8000 6200 81000 188000 86200 80400
  //   400809 400c00 60040 7*40 8000 6200 81000 13*40 8000 6200 81000 13*40 8000 6200 81000 13*40 8000 6200
  //   81000 13*40 8000 6200 81000 13*40 8000 6200 81000 60040 12*40 8000 6200 81000 20 12*40 8000 6200
  //   81000 180400 60040 11*40 8000 6200 81000 200400 60040 11*40 8000 6200 81000 480400 60040 11*40 8000
  //   6200 81000 400809 408800 86200 80400 60040 8*40 8000 6200 81000 400809 408800 182000 80100 60040
  //   8*40 8000 6200 81000 400809 408800 86200 80400 60040 8*40 8000 6200 81000 400809 408800 182000 80100
  //   60040 8*40 8000 6200 81000 400889 400c00 60040 10*40 8000 6200 81000 40088a 400c00 60040 10*40 8000
  //   6200 81000 400889 400c00 60040 10*40 8000 6200 81000 13*40 8000 6200 81000 40088d 400c00 60040 10*40
  //   8000 6200 81000 40088e 400c00 60040 10*40 8000 6200 81000 40088f 400c00 60040 10*40 8000 6200 81000
  //   400890 400c00 60040 10*40 8000 6200 81000 400891 400c00 60040 10*40 8000 6200 81000 400892 400c00
  //   60040 10*40 8000 6200 81000 400893 400c00 60040 10*40 8000 6200 81000 400809 60000 11*40 8000 6200
  //   81000 400809 70000 60040 10*40 8000 6200 81000 70000 60040 11*40 8000 6200 81000 400 470809 400c00
  //   60040 9*40 8000 6200 81000 1c0000 12*40 8000 6200 81000 40080a 400c00 188000 2000 80100 60040 7*40
  //   8000 6200 81000 188000 86200 80400 400809 400c00 60040 7*40 8000 6200 81000 13*40 8000 6200 81000
  //   13*40 8000 6200 81000 13*40 8000 6200 81000 13*40 8000 6200 81000 13*40 8000 6200 81000 60040 12*40
  //   8000 6200 81000 20 12*40 8000 6200 81000 180400 60040 11*40 8000 6200 81000 200400 60040 11*40 8000
  //   6200 81000 480400 60040 11*40 8000 6200 81000 400809 408800 86200 80400 60040 8*40 8000 6200 81000
  //   400809 408800 182000 80100 60040 8*40 8000 6200 81000 400809 408800 86200 80400 60040 8*40 8000 6200
  //   81000 400809 408800 182000 80100 60040 8*40 8000 6200 81000 400889 400c00 60040 10*40 8000 6200
  //   81000 40088a 400c00 60040 10*40 8000 6200 81000 400889 400c00 60040 10*40 8000 6200 81000 13*40 8000
  //   6200 81000 40088d 400c00 60040 10*40 8000 6200 81000 40088e 400c00 60040 10*40 8000 6200 81000
  //   40088f 400c00 60040 10*40 8000 6200 81000 400890 400c00 60040 10*40 8000 6200 81000 400891 400c00
  //   60040 10*40 8000 6200 81000 400892 400c00 60040 10*40 8000 6200 81000 400893 400c00 60040 10*40 8000
  //   6200 81000 400809 70000 60040 10*40 8000 6200 81000 400809 60000 11*40 8000 6200 81000 70000 60040
  //   11*40 8000 6200 81000 400 470809 400c00 60040 9*40 8000 6200 81000 1c0000 12*40 8000 6200 81000
  //   40080a 400c00 188000 2000 80100 60040 7*40 8000 6200 81000 188000 86200 80400 400809 400c00 60040
  //   7*40 8000 6200 81000 13*40 8000 6200 81000 13*40 8000 6200 81000 13*40 8000 6200 81000 13*40 8000
  //   6200 81000 13*40 8000 6200 81000 60040 12*40 8000 6200 81000 20 12*40 8000 6200 81000 180400 60040
  //   11*40 8000 6200 81000 200400 60040 11*40 8000 6200 81000 480400 60040 11*40 8000 6200 81000 400809
  //   408800 86200 80400 60040 8*40 8000 6200 81000 400809 408800 182000 80100 60040 8*40 8000 6200 81000
  //   400809 408800 86200 80400 60040 8*40 8000 62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
endmodule

module extender (
  input  [7:0] imm8,
  input  [4:0] off5,
  input  [7:0] rel8,
  input  [10:0] rel11,
  input  [2:0] Format,
  input  [4:0] opcode,
  output [15:0] in_out
);

  wire comparator_1_gt;
  wire [15:0] bit_extender_1_out, bit_extender_2_out, bit_extender_3_out, bit_extender_4_out,
       bit_extender_5_out, multiplexer_1_out;

  assign bit_extender_1_out = {{8{1'b0}}, imm8};  // Bit_Extender bit_extender_1
  Multiplexer #(.width(16)) multiplexer_1 (
    .in0(bit_extender_2_out), .in1(bit_extender_1_out), .out(multiplexer_1_out), .sel(comparator_1_gt));
  assign bit_extender_2_out = {{8{imm8[7]}}, imm8};  // Bit_Extender bit_extender_2
  assign bit_extender_3_out = {{11{off5[4]}}, off5};  // Bit_Extender bit_extender_3
  assign bit_extender_4_out = {{8{rel8[7]}}, rel8};  // Bit_Extender bit_extender_4
  assign bit_extender_5_out = {{5{rel11[10]}}, rel11};  // Bit_Extender bit_extender_5
  Comparator #(.mode("unsigned"), .width(5)) comparator_1 (
    .a(opcode), .b(5'b01011), .gt(comparator_1_gt), .eq(comparator_1_gt));  // open: lt
  Multiplexer #(.select(3), .width(16)) multiplexer_2 (
    .in3(multiplexer_1_out), .in4(bit_extender_3_out), .in5(bit_extender_4_out), .in6(bit_extender_5_out),
    .out(in_out), .sel(Format));  // open: in0, in1, in2, in7
endmodule
